// Logisim project FullAdderChipV2.circ as structural Verilog: 1 circuit, main circuit main
module main (
  input  I4,
  input  in_2,
  input  I3,
  input  in_4,
  input  ID,
  input  in_6,
  input  IC,
  input  in_8,
  input  I2,
  input  in_10,
  input  I1,
  input  in_12
);

  wire A_out, and_1_out, and_2_out, and_3_out, and_4_out, and_5_out, and_6_out, and_7_out, and_8_out,
       and_9_out, and_10_out, and_11_out, and_12_out, and_13_out, and_14_out, and_15_out, and_16_out, B_out,
       E_out, F_out, nand_1_out, nand_2_out, nand_3_out, nand_4_out, not_1_out, not_2_out, not_3_out,
       not_4_out, or_1_out, or_2_out, or_3_out, or_4_out, or_5_out, or_6_out, or_7_out, or_8_out, or_9_out,
       or_10_out, or_11_out, or_12_out, or_13_out, or_14_out, or_15_out, or_16_out;

  not not_1 (not_1_out, ID);
  not not_2 (not_2_out, IC);
  LED led_1 (.in(I4));
  LED led_2 (.in(I3));
  LED led_3 (.in(not_1_out));
  LED led_4 (.in(not_2_out));
  LED led_5 (.in(I2));
  LED led_6 (.in(I1));
  and and_1 (and_1_out, I4, I3, not_1_out);
  and and_2 (and_2_out, I4, not_1_out, I1);
  and and_3 (and_3_out, I4, I3, not_2_out);
  and and_4 (and_4_out, I3, not_1_out, I2);
  and and_5 (and_5_out, I4, not_1_out, I1);
  and and_6 (and_6_out, I4, I3, not_2_out);
  and and_7 (and_7_out, I3, not_1_out, I2);
  and and_8 (and_8_out, not_2_out, I2, I1);
  and and_9 (and_9_out, I4, I3, not_1_out);
  and and_10 (and_10_out, not_1_out, I2, I1);
  and and_11 (and_11_out, I3, not_2_out, I2);
  and and_12 (and_12_out, I4, not_2_out, I1);
  and and_13 (and_13_out, not_2_out, I2, I1);
  and and_14 (and_14_out, not_1_out, I2, I1);
  and and_15 (and_15_out, I3, not_2_out, I2);
  and and_16 (and_16_out, I4, not_2_out, I1);
  nor F (F_out, and_1_out, and_2_out, and_3_out, and_4_out);
  LED led_7 (.in(F_out));
  nor E (E_out, and_5_out, and_6_out, and_7_out, and_8_out);
  LED led_8 (.in(E_out));
  nor B (B_out, and_9_out, and_10_out, and_11_out, and_12_out);
  LED led_9 (.in(B_out));
  nor A (A_out, and_13_out, and_14_out, and_15_out, and_16_out);
  LED led_10 (.in(A_out));
  not not_3 (not_3_out, in_6);
  not not_4 (not_4_out, in_8);
  LED led_11 (.in(in_2));
  LED led_12 (.in(in_4));
  LED led_13 (.in(in_10));
  LED led_14 (.in(in_12));
  LED led_15 (.in(not_3_out));
  LED led_16 (.in(not_4_out));
  or or_1 (or_1_out, in_2, in_4, not_3_out);
  or or_2 (or_2_out, in_2, not_3_out, in_12);
  or or_3 (or_3_out, in_2, in_4, not_4_out);
  or or_4 (or_4_out, in_4, not_3_out, in_10);
  or or_5 (or_5_out, in_2, not_3_out, in_12);
  or or_6 (or_6_out, in_2, in_4, not_4_out);
  or or_7 (or_7_out, in_4, not_3_out, in_10);
  or or_8 (or_8_out, not_4_out, in_10, in_12);
  or or_9 (or_9_out, in_2, in_4, not_3_out);
  or or_10 (or_10_out, not_3_out, in_10, in_12);
  or or_11 (or_11_out, in_4, not_4_out, in_10);
  or or_12 (or_12_out, in_2, not_4_out, in_12);
  or or_13 (or_13_out, not_4_out, in_10, in_12);
  or or_14 (or_14_out, not_3_out, in_10, in_12);
  or or_15 (or_15_out, in_4, not_4_out, in_10);
  or or_16 (or_16_out, in_2, not_4_out, in_12);
  nand nand_1 (nand_1_out, or_1_out, or_2_out, or_3_out, or_4_out);
  nand nand_2 (nand_2_out, or_5_out, or_6_out, or_7_out, or_8_out);
  nand nand_3 (nand_3_out, or_9_out, or_10_out, or_11_out, or_12_out);
  nand nand_4 (nand_4_out, or_13_out, or_14_out, or_15_out, or_16_out);
  LED led_17 (.in(nand_1_out));
  LED led_18 (.in(nand_2_out));
  LED led_19 (.in(nand_3_out));
  LED led_20 (.in(nand_4_out));
endmodule
