// Logisim project FullAdderChipV3.circ as structural Verilog: 1 circuit, main circuit main
module main (
  input  OPA,
  input  OPB,
  input  OPC
);

  wire nand_1_out, nand_2_out, nand_3_out, nand_4_out, not_1_out, not_2_out, not_3_out, not_4_out, not_5_out,
       or_1_out, or_2_out, or_3_out, or_4_out, or_5_out, or_6_out, or_7_out, or_8_out, or_9_out, or_10_out,
       or_11_out, or_12_out, or_13_out, or_14_out, or_15_out, or_16_out;

  not not_1 (not_1_out, OPA);
  not not_2 (not_2_out, OPB);
  not not_3 (not_3_out, OPC);
  not not_4 (not_4_out, OPC);
  not not_5 (not_5_out, not_3_out);
  LED led_1 (.in(not_1_out));
  LED led_2 (.in(not_2_out));
  LED led_3 (.in(not_4_out));
  LED led_4 (.in(not_5_out));
  LED led_5 (.in(OPA));
  LED led_6 (.in(OPB));
  or or_1 (or_1_out, not_1_out, not_2_out, not_4_out);
  or or_2 (or_2_out, not_1_out, not_4_out, OPB);
  or or_3 (or_3_out, not_1_out, not_2_out, not_5_out);
  or or_4 (or_4_out, not_2_out, not_4_out, OPA);
  or or_5 (or_5_out, not_1_out, not_4_out, OPB);
  or or_6 (or_6_out, not_1_out, not_2_out, not_5_out);
  or or_7 (or_7_out, not_2_out, not_4_out, OPA);
  or or_8 (or_8_out, not_5_out, OPA, OPB);
  or or_9 (or_9_out, not_1_out, not_2_out, not_4_out);
  or or_10 (or_10_out, not_4_out, OPA, OPB);
  or or_11 (or_11_out, not_2_out, not_5_out, OPA);
  or or_12 (or_12_out, not_1_out, not_5_out, OPB);
  or or_13 (or_13_out, not_5_out, OPA, OPB);
  or or_14 (or_14_out, not_4_out, OPA, OPB);
  or or_15 (or_15_out, not_2_out, not_5_out, OPA);
  or or_16 (or_16_out, not_1_out, not_5_out, OPB);
  nand nand_1 (nand_1_out, or_1_out, or_2_out, or_3_out, or_4_out);
  nand nand_2 (nand_2_out, or_5_out, or_6_out, or_7_out, or_8_out);
  nand nand_3 (nand_3_out, or_9_out, or_10_out, or_11_out, or_12_out);
  nand nand_4 (nand_4_out, or_13_out, or_14_out, or_15_out, or_16_out);
  LED QC (.in(nand_4_out));
  LED QS (.in(nand_2_out));
  LED CARRY (.in(nand_1_out));
  LED SUM (.in(nand_3_out));
endmodule
