// Logisim project NewFullAdder.circ as structural Verilog: 1 circuit, main circuit main
module main (
  input  _6,
  input  _8,
  input  _10,
  input  _14,
  input  _15,
  input  _18,
  output A,
  output B,
  output E,
  output F
);

  wire and_1_out, and_2_out, and_3_out, and_4_out, and_5_out, and_6_out, and_7_out, and_8_out, and_9_out,
       and_10_out, and_11_out, and_12_out, and_13_out, and_14_out, and_15_out, and_16_out, not_1_out,
       not_2_out;

  not not_1 (not_1_out, _10);
  not not_2 (not_2_out, _14);
  and and_1 (and_1_out, _18, _15, not_2_out);
  and and_2 (and_2_out, _8, not_2_out, _15, _18);
  and and_3 (and_3_out, _8, not_2_out, _15);
  and and_4 (and_4_out, _6, not_2_out, _18);
  and and_5 (and_5_out, _6, _8, not_1_out);
  and and_6 (and_6_out, _8, not_2_out, _15, _18);
  and and_7 (and_7_out, _8, not_2_out, _15);
  and and_8 (and_8_out, _6, not_2_out, _18);
  and and_9 (and_9_out, _6, _18);
  and and_10 (and_10_out, _8, not_1_out, _15);
  and and_11 (and_11_out, _6, _8, not_2_out);
  and and_12 (and_12_out, not_2_out, _15, _18);
  and and_13 (and_13_out, _6, _8, not_1_out);
  and and_14 (and_14_out, _6, _18);
  and and_15 (and_15_out, _6, _8, not_2_out);
  and and_16 (and_16_out, _8, not_1_out, _15);
  or or_1 (A, and_1_out, and_2_out, and_3_out, and_4_out);
  or or_2 (B, and_5_out, and_6_out, and_7_out, and_8_out);
  or or_3 (E, and_9_out, and_10_out, and_11_out, and_12_out);
  or or_4 (F, and_13_out, and_14_out, and_15_out, and_16_out);
endmodule
